# Fritzing sketch RTC_DATETIME_LED_wiring (saved by Fritzing 0.9.3b)
breadboards: 1

parts:
  Parts1 = SparkFun RedBoard [part_number=DEV-12757]
  Part1 = Adafruit DS3231 [part_number="Adafruit #3013"]

nets:
  N1: Parts1.A4/SDA, Part1.SDA
  N2: Parts1.A5/SCL, Part1.SCL
  N3: Parts1.D2, Part1.SQW
  5V: Parts1.5V, Part1.Vin
  GND: Parts1.GND, Part1.GND

custom parts:
  SparkFun RedBoard: At SparkFun we use many Arduinos and we’re always looking for the simplest, most stable one. Each board is a bit different and no one board has everything we want, so we decided to make our own version that combines all our favorite features. The RedBoard combines the simplicity of the UNO’s Optiboot bootloader (which is used in the Pro series), the stability of the FTDI (which we all missed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
  Adafruit DS3231: The datasheet for the DS3231 explains that this part is an "Extremely Accurate I²C-Integrated RTC/TCXO/Crystal". And, hey, it does exactly what it says on the tin! This Real Time Clock (RTC) is the most precise you can get in a small, low power package. Most RTCs use an external 32kHz timing crystal that is used to keep time with low current draw. And that's all well and good, but those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
