# Fritzing sketch sdCardExample (saved by Fritzing 0.9.3b)

parts:
  Parts1 = SparkFun RedBoard [part_number=DEV-12757]
  Part1 = Adafruit MicroSD card breakout board [part_number="Adafruit #254"]

nets:
  N1: Parts1.D10_PWM/SS, Part1.CS
  N2: Parts1.D11_PWM/MOSI, Part1.DI
  N3: Parts1.D12/MISO, Part1.DO
  N4: Parts1.D13/SCK, Part1.CLK
  GND: Parts1.GND, Part1.GND
  5V: Parts1.5V, Part1.VCC

custom parts:
  SparkFun RedBoard: At SparkFun we use many Arduinos and we’re always looking for the simplest, most stable one. Each board is a bit different and no one board has everything we want, so we decided to make our own version that combines all our favorite features. The RedBoard combines the simplicity of the UNO’s Optiboot bootloader (which is used in the Pro series), the stability of the FTDI (which we all missed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
  Adafruit MicroSD card breakout board: Not just a simple breakout board, this microSD adapter goes the extra mile - designed for ease of use. Onboard 5v->3v regulator provides 150mA for power-hungry cards 3v level shifting means you can use this with ease on either 3v or 5v systems Uses a proper level shifting chip, not resistors: less problems, and faster read/write access Use 3 or 4 digital pins to read and write 2Gb+ of storage!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
