# Fritzing sketch megaSensorFritzing (saved by Fritzing 0.9.3b)
breadboards: 1

parts:
  Part1 = Arduino Mega 2560 (Rev3)
  DHT1 = DHT22 Humidity and Temperature Sensor
  Part2 = Adafruit MicroSD card breakout board [part_number="Adafruit #254"]
  Part4 = Adafruit MAX4466 Electret Microphone Amplifier [part_number="Adafruit #1063"]
  Part6 = Adafruit TSL2561 [part_number="Adafruit #439"]
  Part7 = Adafruit DS3231 [part_number="Adafruit #3013"]
  PIR1 = PIR sensor
  R1 = Resistor [tolerance=±5% resistance=10k package="0603 [SMD]"]
  R2 = Resistor [tolerance=±5% resistance=220 package="0603 [SMD]"]
  LED1 = smd LED [color="Red (633nm)" package="0603 [SMD]"]

nets:
  N1: Part1.A0, Part4.OUT
  N2: Part1.D21/SCL, Part6.SCL, Part7.SCL
  N3: Part1.D20/SDA, Part6.SDA, Part7.SDA
  N4: Part1.D10_PWM, PIR1.SIG
  N5: Part1.D8_PWM, R2.Pin_1
  3V3: Part1.3V3, Part4.VCC
  VDD: Part1.5V, DHT1.VDD, Part2.+3V3, Part6.VIN, Part7.Vin, PIR1.VDD, R1.Pin_1
  GND: Part1.GND, DHT1.GND, Part2.GND, Part4.GND, Part6.GND, Part7.GND, PIR1.GND, LED1.cathode
  N6: Part1.D2_PWM, Part7.SQW
  N7: Part1.D3_PWM, DHT1.DATA, R1.Pin_0
  N8: Part1.D50, Part2.DO
  N9: Part1.D51, Part2.DI
  N10: Part1.D52, Part2.CLK
  N11: Part1.D53, Part2.CS
  N12: R2.Pin_0, LED1.anode

custom parts:
  Adafruit MicroSD card breakout board: Not just a simple breakout board, this microSD adapter goes the extra mile - designed for ease of use. Onboard 5v->3v regulator provides 150mA for power-hungry cards 3v level shifting means you can use this with ease on either 3v or 5v systems Uses a proper level shifting chip, not resistors: less problems, and faster read/write access Use 3 or 4 digital pins to read and write 2Gb+ of storage!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
  Adafruit MAX4466 Electret Microphone Amplifier: Add an ear to your project with this well-designed electret microphone amplifier. This fully assembled and tested board comes with a 20-20KHz electret microphone soldered on. For the amplification, we use the Maxim MAX4466, an op-amp specifically designed for this delicate task! The amplifier has excellent power supply noise rejection, so this amplifier sounds really good and isn't nearly as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
  Adafruit TSL2561: The TSL2561 luminosity sensor is an advanced digital light sensor, ideal for use in a wide range of light situations. Compared to low cost CdS cells, this sensor is more precise, allowing for exact lux calculations and can be configured for different gain/timing ranges to detect light ranges from up to 0.1 - 40,000+ Lux on the fly. The best part of this sensor is that it contains both infrared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
  Adafruit DS3231: The datasheet for the DS3231 explains that this part is an "Extremely Accurate I²C-Integrated RTC/TCXO/Crystal". And, hey, it does exactly what it says on the tin! This Real Time Clock (RTC) is the most precise you can get in a small, low power package. Most RTCs use an external 32kHz timing crystal that is used to keep time with low current draw. And that's all well and good, but those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
